# Fritzing sketch Diagrama fritzing (saved by Fritzing 0.9.3b)
breadboards: 1

parts:
  PIR1 = PIR sensor
  Composant1 = Arduino Uno (Rev3)
  S2 = Pushbutton [package="[THT]"]
  LED1 = LED - 5mm [color="Red (633nm)" package="5 mm [THT]"]
  LED2 = LED - 5mm [color="Red (633nm)" package="5 mm [THT]"]
  LED3 = LED - 5mm [color="Green (570nm)" package="5 mm [THT]"]
  J1 = Piezo Speaker
  R1 = Resistor [tolerance=±5% resistance=220 package=THT]
  R2 = Resistor [tolerance=±5% resistance=220 package=THT]
  R3 = Resistor [tolerance=±5% resistance=220 package=THT]
  R6 = Resistor [tolerance=±5% resistance=220 package=THT]
  Part3 = RFID-RC522-v2
  U1 = GAS_SENSOR [package=mq-3]
  R7 = Resistor [tolerance=±5% resistance=22 package=THT]  # not connected

nets:
  VDD: PIR1.VDD, Composant1.5V, S2.Pin_1, S2.Pin_2, U1.A1, U1.H1, U1.H2
  N1: PIR1.SIG, Composant1.D2
  GND: PIR1.GND, Composant1.GND, R1.Pin_0, R2.Pin_0, R3.Pin_0, R6.Pin_0, Part3.GND
  N2: Composant1.A0, U1.B1
  N3: Composant1.D8, LED3.anode
  N4: Composant1.D10_PWM/SS, Part3.SDA
  N5: Composant1.D11_PWM/MOSI, Part3.MOSI
  N6: Composant1.D12/MISO, Part3.MISO
  N7: Composant1.D13/SCK, Part3.SCK
  N8: Composant1.D3_PWM, LED1.anode
  N9: Composant1.D5_PWM, Part3.RST
  N10: Composant1.D6_PWM, S2.Pin_3, S2.Pin_4, R6.Pin_1
  N11: Composant1.D7, J1.pin2
  N12: Composant1.3V3, Part3.3_3V
  N13: LED1.cathode, R3.Pin_1
  N14: LED2.cathode, R2.Pin_1
  N15: LED3.cathode, R1.Pin_1

custom parts:
  RFID-RC522-v2: A simple China made RFID-RC522 Reader; do check the pin labels, as this is a MFRC522 based clone.

// code stored in the sketch: pir_sensor.ino
/*Ahram Canadian University
Course project*/
int pir =2;
int pirState;
int red1=3;
int red2=4;
int green=5;
int pushbutton1=6;
int pushbutton2=7;
int pushbutton3=8;
int count1;
int count2;
int count3;
int speaker=9;


void setup() {
  // put your setup code here, to run once:
  pinMode(pir, INPUT);
  pinMode(red1, OUTPUT);
  pinMode(red2, OUTPUT);
  pinMode(green, OUTPUT);
  pinMode(pushbutton1, INPUT);
  pinMode(pushbutton2, INPUT);
  pinMode(pushbutton3, INPUT);
  pinMode(speaker, OUTPUT);
  pirState=LOW;
}

void loop() {
  // put your main code here, to run repeatedly:
  
  pirState = digitalRead(pir);
  
  if(pirState==HIGH){
    if(count1==1&&count2==2&&count3==1;){
        stopalarm();
        count1=0;
        count2=0;
        count3=0;
      }
      else{
        alarm();
        if(digitalRead(pushbutton1)==LOW){
            count1+=1;
          }
        else if(digitalRead(pushbutton2)==LOW){
            count2+=1;
          }
        else if(digitalRead(pushbutton3)==LOW){
            count3+=1;      
          }
      } 
  }
  else{
    stopalarm();
  }      
}
void alarm(long duration, int frequency){
  
  digitalWrite(red1, HIGH);
  delay(200);
  digitalWrite(red2, HIGH);
  delay(200);
  play(300, 160);
}

void play(long duration, int frequency){
  duration = duration*1000;
  int period = (1.0/frequency)*1000000;
  long elapsed = 0;
  while(elapsed<duration){
    digitalWrite(speaker, HIGH);
    delayMicroseconds(period/2);
    digitalWrite(speaker, LOW);
    delayMicroseconds(period/2);
    elapsed+= period;
  }
}

void stopalarm(){
  digitalWrite(red1, LOW);
  digitalWrite(red2, LOW);
  digitalWrite(green, HIGH); 
  delay(500);
}
