# Fritzing sketch Sensor_PIR_con_buzzer (saved by Fritzing 0.9.2b)
breadboards: 1

parts:
  PIR1 = PIR sensor
  Composant1 = Arduino Uno (Rev3)
  S1 = Pushbutton [package="[THT]"]
  S2 = Pushbutton [package="[THT]"]
  S3 = Pushbutton [package="[THT]"]
  LED1 = LED - 5mm [color="Red (633nm)" package="5 mm [THT]"]
  LED2 = LED - 5mm [color="Red (633nm)" package="5 mm [THT]"]
  LED3 = LED - 5mm [color="Green (570nm)" package="5 mm [THT]"]
  J1 = Piezo Speaker
  R1 = Resistor [tolerance=±5% resistance=220 package=THT]
  R2 = Resistor [tolerance=±5% resistance=220 package=THT]
  R3 = Resistor [tolerance=±5% resistance=220 package=THT]
  R4 = Resistor [tolerance=±5% resistance=220 package=THT]
  R5 = Resistor [tolerance=±5% resistance=220 package=THT]
  R6 = Resistor [tolerance=±5% resistance=220 package=THT]

nets:
  VDD: PIR1.VDD, Composant1.5V, S1.Pin_1, S1.Pin_2, S2.Pin_1, S2.Pin_2, S3.Pin_1, S3.Pin_2
  N1: PIR1.SIG, Composant1.D2
  GND: PIR1.GND, Composant1.GND, J1.pin1, R1.Pin_0, R2.Pin_0, R3.Pin_0, R4.Pin_0, R5.Pin_0, R6.Pin_0
  N2: Composant1.D8, S3.Pin_3, S3.Pin_4, R4.Pin_1
  N3: Composant1.D9_PWM, J1.pin2
  N4: Composant1.D3_PWM, LED1.anode
  N5: Composant1.D4, LED2.anode
  N6: Composant1.D5_PWM, LED3.anode
  N7: Composant1.D6_PWM, S1.Pin_3, S1.Pin_4, R5.Pin_1
  N8: Composant1.D7, S2.Pin_3, S2.Pin_4, R6.Pin_1
  N9: LED1.cathode, R3.Pin_1
  N10: LED2.cathode, R2.Pin_1
  N11: LED3.cathode, R1.Pin_1

// code stored in the sketch: pir_sensor.ino
/*Ahram Canadian University
Course project*/
int pir =2;
int pirState;
int red1=3;
int red2=4;
int green=5;
int pushbutton1=6;
int pushbutton2=7;
int pushbutton3=8;
int count1;
int count2;
int count3;
int speaker=9;


void setup() {
  // put your setup code here, to run once:
  pinMode(pir, INPUT);
  pinMode(red1, OUTPUT);
  pinMode(red2, OUTPUT);
  pinMode(green, OUTPUT);
  pinMode(pushbutton1, INPUT);
  pinMode(pushbutton2, INPUT);
  pinMode(pushbutton3, INPUT);
  pinMode(speaker, OUTPUT);
  pirState=LOW;
}

void loop() {
  // put your main code here, to run repeatedly:
  
  pirState = digitalRead(pir);
  
  if(pirState==HIGH){
    if(count1==1&&count2==2&&count3==1;){
        stopalarm();
        count1=0;
        count2=0;
        count3=0;
      }
      else{
        alarm();
        if(digitalRead(pushbutton1)==LOW){
            count1+=1;
          }
        else if(digitalRead(pushbutton2)==LOW){
            count2+=1;
          }
        else if(digitalRead(pushbutton3)==LOW){
            count3+=1;      
          }
      } 
  }
  else{
    stopalarm();
  }      
}
void alarm(long duration, int frequency){
  
  digitalWrite(red1, HIGH);
  delay(200);
  digitalWrite(red2, HIGH);
  delay(200);
  play(300, 160);
}

void play(long duration, int frequency){
  duration = duration*1000;
  int period = (1.0/frequency)*1000000;
  long elapsed = 0;
  while(elapsed<duration){
    digitalWrite(speaker, HIGH);
    delayMicroseconds(period/2);
    digitalWrite(speaker, LOW);
    delayMicroseconds(period/2);
    elapsed+= period;
  }
}

void stopalarm(){
  digitalWrite(red1, LOW);
  digitalWrite(red2, LOW);
  digitalWrite(green, HIGH); 
  delay(500);
}
